# Fritzing sketch Car LED Controller (saved by Fritzing 0.9.10b)
breadboards: 2

parts:
  U2 = LCD-16X2 [package=lcd-16x2_noholes]
  U3 = POT [knob_status=50% power=0.5W package=alps_pot]
  C1 = Capacitor [package=cap-pth-small2]
  C2 = Capacitor [package=cap-pth-small2]
  C3 = Capacitor [package=cap-pth-small2]
  C4 = Capacitor [package=cap-pth-small2]
  S2 = Momentary Switch [package=ksa_sealed_tac_switch]
  R10 = Resistor [tolerance=±5% resistance=1M package="1206 [SMD]"]
  M1 = RioRand LM2596
  M2 = RioRand LM2596
  JP1 = Header 4 [package=molex-1x4_lock]
  U6 = SK6812 RGBW LED Strip
  R11 = Resistor [tolerance=±5% power=0.25 resistance=47k package=THT]
  R12 = Resistor [tolerance=±5% power=0.25 resistance=47k package=THT]
  R13 = Resistor [tolerance=±5% power=0.25 resistance=47k package=THT]
  R14 = Resistor [tolerance=±5% power=0.25 resistance=47k package=THT]
  R15 = Resistor [tolerance=±5% power=0.25 resistance=1M package=THT]
  R16 = Resistor [tolerance=±5% power=0.25 resistance=1M package=THT]
  R17 = Resistor [tolerance=±5% power=0.25 resistance=1M package=THT]
  R18 = Resistor [tolerance=±5% power=0.25 resistance=1M package=THT]
  Power_plug1 = Power plug
  M3 = DOIT Esp32 DevKit v1 (30 pins long, 11 pins width) [part_number=ESP32S-PIN30]

nets:
  N1: U2.VSS, U2.R_W, U2.K, U3.E, C1.1, C2.1, C3.1, C4.1, R10.Pin_0, M2.Pin_4, R11.Pin_0, R12.Pin_0, R13.Pin_0, R14.Pin_0
  N2: U2.VDD, U2.A, U3.A, M2.Pin_3
  N3: U2.VO, U3.S
  N4: U2.RS, M3.D32
  N5: U2.E, M3.D33
  N6: U2.DB4, M3.D25
  N7: U2.DB5, M3.D26
  N8: U2.DB6, M3.D27
  N9: U2.DB7, M3.D14
  N10: C1.2, R14.Pin_1, R18.Pin_0, M3.D35
  N11: C2.2, R11.Pin_1, R17.Pin_0, M3.VP
  N12: C3.2, R12.Pin_1, R15.Pin_0, M3.VN
  N13: C4.2, R13.Pin_1, R16.Pin_0, M3.D34
  N14: S2.1, S2.2, R10.Pin_1, M3.D22
  N15: S2.3, S2.4, M3.TX0
  N16: M1.Pin_1, M2.Pin_1, Power_plug1.VCC
  N17: M1.Pin_2, M2.Pin_2, Power_plug1.GND
  N18: M1.Pin_3, U6.+5V
  N19: M1.Pin_4, U6.GND#0
  N20: JP1.1, R17.Pin_1
  N21: JP1.2, R15.Pin_1
  N22: JP1.3, R16.Pin_1
  N23: JP1.4, R18.Pin_1
  N24: U6.Din, U6.GND#3, M3.D23

custom parts:
  SK6812 RGBW LED Strip: SK6812 RGBW Strip
  DOIT Esp32 DevKit v1 (30 pins long, 11 pins width): The DOIT Esp32 DevKit v1 is one of the development board created by DOIT to evaluate the ESP-WROOM-32 module. It is based on the ESP32 microcontroller that boasts Wifi, Bluetooth, Ethernet and Low Power support all in a single chip. (vanepp) made breadboard work, adjusted pin numbering and labels and reduced size of schematic and cleaned up pcb. This chip is 30pins long (2 x15) and 11 pins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
